# Fritzing sketch CatanDice (saved by Fritzing 0.9.6b)

parts:
  Mod1 = rpi_pico-tht_1
  LCD1 = TFT 1.8 inch 160x128 w SD
  SW = ENCODER_AB [package=encoder_led_3]
  C1 = Capacitor [package=cap-pth-large]
  R1 = Resistor [tolerance=±5% power=0.25 resistance=10k package=THT]
  R2 = Resistor [tolerance=±5% power=0.25 resistance=10k package=THT]
  R3 = Resistor [tolerance=±5% power=0.25 resistance=10k package=THT]
  C2 = Capacitor [package=cap-pth-large]
  C3 = Capacitor [package=cap-pth-large]
  Q1 = TRANSISTOR_NPN [package=to-92]
  J1 = Piezo Speaker
  R4 = Resistor [tolerance=±5% power=0.25 resistance=10k package=THT]

nets:
  N1: Mod1.connector2, SW.P1, SW.G, C1.2, C2.2, C3.2, Q1.E
  N2: Mod1.connector3, LCD1.pin_5
  N3: Mod1.connector4, LCD1.pin_4
  N4: Mod1.connector6, LCD1.pin_2
  N5: Mod1.connector7, LCD1.pin_8
  N6: Mod1.connector8, R4.Pin_0
  N7: Mod1.connector9, C1.1, R1.Pin_0
  N8: Mod1.connector10, R3.Pin_0, C2.1
  N9: Mod1.connector11, R2.Pin_0, C3.1
  N10: Mod1.connector13, LCD1.pin_1
  N11: Mod1.connector14, LCD1.pin_3
  N12: Mod1.connector20, LCD1.pin_10
  N13: Mod1.connector21, LCD1.pin_12
  N14: Mod1.connector23, LCD1.pin_9
  N15: Mod1.connector24, LCD1.pin_11
  N16: Mod1.connector28, LCD1.pin_7
  N17: Mod1.connector35, LCD1.pin_6
  N18: Mod1.connector39, J1.pin2
  N19: SW.P2, R1.Pin_1
  N20: SW.A, R3.Pin_1
  N21: SW.B, R2.Pin_1
  N22: Q1.B, R4.Pin_1
  N23: Q1.C, J1.pin1

custom parts:
  TFT 1.8 inch 160x128 w SD: This is a generic 1.8 tft spi lcd display available on ebay and others. The 1.8" display has 128x160 color pixels china version
  ENCODER_AB: Rotary Encoder and select switch EC12PLRGBSDVBF-D: http://top-up.so-buy.com/front/bin/ptdetail.phtml?Part=EC12PLRGBSDVBF-D
